# Fritzing sketch Multiplexing 74HC595AnalogInput (saved by Fritzing 0.9.2b)
breadboards: 2

parts:
  Arduino_Uno = Arduino Uno (Rev3)
  LED1 = LED - 5mm [color="Red (633nm)" package="5 mm [THT]"]
  LED2 = LED - 5mm [color="Red (633nm)" package="5 mm [THT]"]
  LED3 = LED - 5mm [color="Red (633nm)" package="5 mm [THT]"]
  LED4 = LED - 5mm [color="Red (633nm)" package="5 mm [THT]"]
  LED5 = LED - 5mm [color="Red (633nm)" package="5 mm [THT]"]
  LED6 = LED - 5mm [color="Red (633nm)" package="5 mm [THT]"]
  LED7 = LED - 5mm [color="Red (633nm)" package="5 mm [THT]"]
  LED8 = LED - 5mm [color="Red (633nm)" package="5 mm [THT]"]
  LED9 = LED - 5mm [color="Red (633nm)" package="5 mm [THT]"]
  LED10 = LED - 5mm [color="Red (633nm)" package="5 mm [THT]"]
  LED11 = LED - 5mm [color="Red (633nm)" package="5 mm [THT]"]
  LED12 = LED - 5mm [color="Red (633nm)" package="5 mm [THT]"]
  LED13 = LED - 5mm [color="Red (633nm)" package="5 mm [THT]"]
  LED14 = LED - 5mm [color="Red (633nm)" package="5 mm [THT]"]
  LED15 = LED - 5mm [color="Red (633nm)" package="5 mm [THT]"]
  LED16 = LED - 5mm [color="Red (633nm)" package="5 mm [THT]"]
  T4HC595_A = 74HC595 [package="DIP16 [THT]"]
  R1 = Resistor [tolerance=±5% resistance=220 package=THT]
  R2 = Resistor [tolerance=±5% resistance=220 package=THT]
  R3 = Resistor [tolerance=±5% resistance=220 package=THT]
  R4 = Resistor [tolerance=±5% resistance=220 package=THT]
  R5 = Resistor [tolerance=±5% resistance=220 package=THT]
  R6 = Resistor [tolerance=±5% resistance=220 package=THT]
  R7 = Resistor [tolerance=±5% resistance=220 package=THT]
  R8 = Resistor [tolerance=±5% resistance=220 package=THT]
  R9 = Resistor [tolerance=±5% resistance=220 package=THT]
  R10 = Resistor [tolerance=±5% resistance=220 package=THT]
  R11 = Resistor [tolerance=±5% resistance=220 package=THT]
  R12 = Resistor [tolerance=±5% resistance=220 package=THT]
  R13 = Resistor [tolerance=±5% resistance=220 package=THT]
  R14 = Resistor [tolerance=±5% resistance=220 package=THT]
  R15 = Resistor [tolerance=±5% resistance=220 package=THT]
  R16 = Resistor [tolerance=±5% resistance=220 package=THT]
  T4HC595_B = 74HC595 [package="DIP16 [THT]"]
  Potentiometer = Rotary Potentiometer (Small) [maximum_resistance=10kΩ package=THT]

nets:
  N1: Arduino_Uno.A0, Potentiometer.wiper
  N2: Arduino_Uno.D8, T4HC595_A.ST_CP, T4HC595_B.ST_CP
  N3: Arduino_Uno.D11_PWM/MOSI, T4HC595_A.DS
  N4: Arduino_Uno.D12/MISO, T4HC595_A.SH_CP, T4HC595_B.SH_CP
  GND: Arduino_Uno.GND, LED1.cathode, LED2.cathode, LED3.cathode, LED4.cathode, LED5.cathode, LED6.cathode, LED7.cathode, LED8.cathode, LED9.cathode, LED10.cathode, LED11.cathode, LED12.cathode, LED13.cathode, LED14.cathode, LED15.cathode, LED16.cathode, T4HC595_A.GND, T4HC595_B.GND, T4HC595_B.OE, Potentiometer.leg2
  VCC: Arduino_Uno.5V, T4HC595_A.MR, T4HC595_A.OE, T4HC595_A.VCC, T4HC595_B.MR, T4HC595_B.VCC, Potentiometer.leg1
  N5: LED1.anode, R1.Pin_0
  N6: LED2.anode, R2.Pin_0
  N7: LED3.anode, R3.Pin_0
  N8: LED4.anode, R4.Pin_0
  N9: LED5.anode, R5.Pin_0
  N10: LED6.anode, R6.Pin_0
  N11: LED7.anode, R7.Pin_0
  N12: LED8.anode, R8.Pin_0
  N13: LED9.anode, R9.Pin_0
  N14: LED10.anode, R10.Pin_0
  N15: LED11.anode, R11.Pin_0
  N16: LED12.anode, R12.Pin_0
  N17: LED13.anode, R13.Pin_0
  N18: LED14.anode, R14.Pin_0
  N19: LED15.anode, R15.Pin_0
  N20: LED16.anode, R16.Pin_0
  N21: T4HC595_A.Q1, R2.Pin_1
  N22: T4HC595_A.Q2, R3.Pin_1
  N23: T4HC595_A.Q3, R4.Pin_1
  N24: T4HC595_A.Q4, R5.Pin_1
  N25: T4HC595_A.Q5, R6.Pin_1
  N26: T4HC595_A.Q6, R7.Pin_1
  N27: T4HC595_A.Q7, R8.Pin_1
  N28: T4HC595_A.Q7', T4HC595_B.DS
  N29: T4HC595_A.Q0, R1.Pin_1
  N30: R9.Pin_1, T4HC595_B.Q0
  N31: R10.Pin_1, T4HC595_B.Q1
  N32: R11.Pin_1, T4HC595_B.Q2
  N33: R12.Pin_1, T4HC595_B.Q3
  N34: R13.Pin_1, T4HC595_B.Q4
  N35: R14.Pin_1, T4HC595_B.Q5
  N36: R15.Pin_1, T4HC595_B.Q6
  N37: R16.Pin_1, T4HC595_B.Q7
